# Fritzing sketch Test Kit 1 (saved by Fritzing 0.9.2b)
circuit board: 8.46667cm x 5.64444cm
breadboards: 1

parts:
  Part1 = Arduino Nano (Rev3.0) (ICSP)
  LED1 = LED - 3mm [color="Green (560nm)" package="3 mm [THT]"]
  LED2 = LED - 3mm [color="Red (633nm)" package="3 mm [THT]"]
  R1 = Resistor [tolerance=±5% resistance=1k package=THT]
  R2 = Resistor [tolerance=±5% resistance=1k package=THT]

nets:
  N1: Part1.GND, R1.Pin_1, R2.Pin_1
  N2: Part1.D3, LED2.anode
  N3: Part1.D5, LED1.anode
  N4: LED1.cathode, R2.Pin_0
  N5: LED2.cathode, R1.Pin_0
